# Fritzing sketch Aurora (saved by Fritzing 0.8.7b)
breadboards: 1

parts:
  Part1 = Arduino Uno (Rev3)
  LED1 = RGB LED (com. anode, rbg) [package="5 mm [THT]"]
  LED2 = RGB LED (com. anode, rbg) [package="5 mm [THT]"]
  R1 = Resistor [tolerance=±5% resistance=220 package=THT]
  R2 = Resistor [tolerance=±5% resistance=220 package=THT]
  R3 = Resistor [tolerance=±5% resistance=220 package=THT]
  R4 = Resistor [tolerance=±5% resistance=220 package=THT]
  R5 = Resistor [tolerance=±5% resistance=220 package=THT]
  R6 = Resistor [tolerance=±5% resistance=220 package=THT]
  R7 = Photocell (LDR) [package=THT]
  R8 = Resistor [tolerance=±5% resistance=220 package=THT]

nets:
  N1: Part1.A0, R7.pin_1, R8.Pin_1
  N2: Part1.D9_PWM, R5.Pin_1
  N3: Part1.D10_PWM/SS, R4.Pin_1
  N4: Part1.D11_PWM/MOSI, R6.Pin_1
  N5: Part1.GND, R8.Pin_0
  N6: Part1.D3_PWM, R1.Pin_1
  N7: Part1.D5_PWM, R2.Pin_1
  N8: Part1.D6_PWM, R3.Pin_1
  N9: Part1.D7, LED1.common_anode, LED2.common_anode
  N10: Part1.5V, R7.pin_0
  N11: LED1.red_cathode, R3.Pin_0
  N12: LED1.blue_cathode, R2.Pin_0
  N13: LED1.green_cathode, R1.Pin_0
  N14: LED2.red_cathode, R6.Pin_0
  N15: LED2.blue_cathode, R5.Pin_0
  N16: LED2.green_cathode, R4.Pin_0
